// Logisim project branch-comp.circ as structural Verilog: 1 circuit, main circuit branch_comp
module branch_comp (
  input  [31:0] rs1,
  input  [31:0] rs2,
  input  BrUn,
  output BrEq,
  output BrLt
);

  wire comparator_1_lt, comparator_2_lt, comparator_3_eq, comparator_4_eq, comparator_4_lt;

  Comparator #(.width(32)) comparator_1 (.a(rs1), .b(rs2), .lt(comparator_1_lt));  // open: gt, eq
  Comparator #(.mode("unsigned"), .width(32)) comparator_2 (.a(rs1), .b(rs2), .lt(comparator_2_lt));  // open: gt, eq
  Comparator #(.width(32)) comparator_3 (.a(rs1), .b(rs2), .eq(comparator_3_eq));  // open: gt, lt
  Comparator #(.mode("unsigned"), .width(32)) comparator_4 (
    .a(rs1), .b(rs2), .eq(comparator_4_eq), .lt(comparator_4_lt));  // open: gt
  Multiplexer #(.enable("false")) multiplexer_1 (.in0(comparator_1_lt), .in1(comparator_2_lt), .out(BrLt), .sel(BrUn));
  Multiplexer #(.enable("false")) multiplexer_2 (.in0(comparator_3_eq), .in1(comparator_4_eq), .out(BrEq), .sel(BrUn));

  // Notes on the sheet:
  //   INPUTS to your circuit
  //   DON'T CHANGE THE LOCATIONS OF THE INPUTS AND OUTPUTS!
  //   OUTPUT from your circuit
endmodule
