// Logisim project control-logic.circ as structural Verilog: 1 circuit, main circuit control_logic
module control_logic (
  input  [31:0] inst,
  input  BrEq,
  input  BrLt,
  output PCSel,
  output RegWEn,
  output [2:0] ImmSel,
  output BrUn,
  output ASel,
  output BSel,
  output [3:0] ALUSel,
  output MemRW,
  output [1:0] WBSel,
  output CSRSel,
  output CSRWen
);

  wire and_1_out, and_2_out, and_3_out, bitselector_1_out, bitselector_2_out, bitselector_3_out,
       bitselector_4_out, bitselector_5_out, is_add, is_addi, is_and, is_andi, is_auipc, is_beq, is_bge,
       is_bgeu, is_blt, is_bltu, is_bne, is_csrw, is_csrwi, is_jal, is_jalr, is_lb, is_lh, is_lui, is_lw,
       is_mul, is_mulh, is_mulhu, is_or, is_ori, is_sb, is_sh, is_sll, is_slli, is_slt, is_slti, is_sra,
       is_srai, is_srl, is_srli, is_sub, is_sw, is_xor, is_xori, not_1_out, not_2_out, or_1_out, or_2_out,
       pri1_on, xor_1_out, xor_2_out;
  wire [2:0] priority_encoder_2_out;
  wire [4:0] priority_encoder_1_out;
  wire [5:0] bit_extender_3_out, pri_out, pri_out2, ROM_in;
  wire [6:0] opcode;

  Bit_Extender #(.in_width(32), .out_width(7)) bit_extender_1 (.in(inst), .out(opcode));
  Comparator #(.width(10)) comparator_1 (.a({inst[14:12], inst[6:0]}), .b(10'h63), .eq(is_beq));  // open: gt, lt
  Comparator #(.width(10)) comparator_2 (.a({inst[14:12], inst[6:0]}), .b(10'he3), .eq(is_bne));  // open: gt, lt
  Comparator #(.width(10)) comparator_3 (.a({inst[14:12], inst[6:0]}), .b(10'h263), .eq(is_blt));  // open: gt, lt
  Comparator #(.width(10)) comparator_4 (.a({inst[14:12], inst[6:0]}), .b(10'h2e3), .eq(is_bge));  // open: gt, lt
  Comparator #(.width(10)) comparator_5 (.a({inst[14:12], inst[6:0]}), .b(10'h363), .eq(is_bltu));  // open: gt, lt
  Comparator #(.width(10)) comparator_6 (.a({inst[14:12], inst[6:0]}), .b(10'h3e3), .eq(is_bgeu));  // open: gt, lt
  Comparator #(.width(7)) comparator_7 (.a(opcode), .b(7'b0010111), .eq(is_auipc));  // open: gt, lt
  Comparator #(.width(7)) comparator_8 (.a(opcode), .b(7'b0110111), .eq(is_lui));  // open: gt, lt
  Comparator #(.width(7)) comparator_9 (.a(opcode), .b(7'b1101111), .eq(is_jal));  // open: gt, lt
  Comparator #(.width(10)) comparator_10 (.a({inst[14:12], inst[6:0]}), .b(10'h67), .eq(is_jalr));  // open: gt, lt
  Comparator #(.width(10)) comparator_11 (.a({inst[14:12], inst[6:0]}), .b(10'hf3), .eq(is_csrw));  // open: gt, lt
  Comparator #(.width(10)) comparator_12 (.a({inst[14:12], inst[6:0]}), .b(10'h2f3), .eq(is_csrwi));  // open: gt, lt
  ROM #(.addrWidth(6), .dataWidth(16)) rom_1 (
    .addr(ROM_in), .data({RegWEn, ImmSel, BrUn, ASel, BSel, ALUSel, MemRW, WBSel, CSRSel, CSRWen}));
  Comparator #(.width(10)) comparator_13 (.a({inst[14:12], inst[6:0]}), .b(10'h13), .eq(is_addi));  // open: gt, lt
  Comparator #(.width(10)) comparator_14 (.a({inst[14:12], inst[6:0]}), .b(10'h93), .eq(is_slli));  // open: gt, lt
  Comparator #(.width(10)) comparator_15 (.a({inst[14:12], inst[6:0]}), .b(10'h113), .eq(is_slti));  // open: gt, lt
  Comparator #(.width(10)) comparator_16 (.a({inst[14:12], inst[6:0]}), .b(10'h213), .eq(is_xori));  // open: gt, lt
  Comparator #(.width(17)) comparator_17 (
    .a({inst[31:25], inst[14:12], inst[6:0]}), .b(17'h293), .eq(is_srli));  // open: gt, lt
  Comparator #(.width(10)) comparator_18 (.a({inst[14:12], inst[6:0]}), .b(10'h313), .eq(is_ori));  // open: gt, lt
  Comparator #(.width(10)) comparator_19 (.a({inst[14:12], inst[6:0]}), .b(10'h393), .eq(is_andi));  // open: gt, lt
  Comparator #(.width(17)) comparator_20 (
    .a({inst[31:25], inst[14:12], inst[6:0]}), .b(17'h8293), .eq(is_srai));  // open: gt, lt
  Comparator #(.width(10)) comparator_21 (.a({inst[14:12], inst[6:0]}), .b(10'h3), .eq(is_lb));  // open: gt, lt
  Comparator #(.width(10)) comparator_22 (.a({inst[14:12], inst[6:0]}), .b(10'h83), .eq(is_lh));  // open: gt, lt
  Comparator #(.width(10)) comparator_23 (.a({inst[14:12], inst[6:0]}), .b(10'h103), .eq(is_lw));  // open: gt, lt
  Comparator #(.width(10)) comparator_24 (.a({inst[14:12], inst[6:0]}), .b(10'h23), .eq(is_sb));  // open: gt, lt
  Comparator #(.width(10)) comparator_25 (.a({inst[14:12], inst[6:0]}), .b(10'ha3), .eq(is_sh));  // open: gt, lt
  Comparator #(.width(10)) comparator_26 (.a({inst[14:12], inst[6:0]}), .b(10'h123), .eq(is_sw));  // open: gt, lt
  Comparator #(.width(17)) comparator_27 (
    .a({inst[31:25], inst[14:12], inst[6:0]}), .b(17'h33), .eq(is_add));  // open: gt, lt
  Comparator #(.width(17)) comparator_28 (
    .a({inst[31:25], inst[14:12], inst[6:0]}), .b(17'h433), .eq(is_mul));  // open: gt, lt
  Comparator #(.width(17)) comparator_29 (
    .a({inst[31:25], inst[14:12], inst[6:0]}), .b(17'h8033), .eq(is_sub));  // open: gt, lt
  Comparator #(.width(17)) comparator_30 (
    .a({inst[31:25], inst[14:12], inst[6:0]}), .b(17'hb3), .eq(is_sll));  // open: gt, lt
  Comparator #(.width(17)) comparator_31 (
    .a({inst[31:25], inst[14:12], inst[6:0]}), .b(17'h4b3), .eq(is_mulh));  // open: gt, lt
  Comparator #(.width(17)) comparator_32 (
    .a({inst[31:25], inst[14:12], inst[6:0]}), .b(17'h5b3), .eq(is_mulhu));  // open: gt, lt
  Comparator #(.width(17)) comparator_33 (
    .a({inst[31:25], inst[14:12], inst[6:0]}), .b(17'h133), .eq(is_slt));  // open: gt, lt
  Comparator #(.width(17)) comparator_34 (
    .a({inst[31:25], inst[14:12], inst[6:0]}), .b(17'h233), .eq(is_xor));  // open: gt, lt
  Comparator #(.width(17)) comparator_35 (
    .a({inst[31:25], inst[14:12], inst[6:0]}), .b(17'h2b3), .eq(is_srl));  // open: gt, lt
  Comparator #(.width(17)) comparator_36 (
    .a({inst[31:25], inst[14:12], inst[6:0]}), .b(17'h82b3), .eq(is_sra));  // open: gt, lt
  Comparator #(.width(17)) comparator_37 (
    .a({inst[31:25], inst[14:12], inst[6:0]}), .b(17'h333), .eq(is_or));  // open: gt, lt
  Comparator #(.width(17)) comparator_38 (
    .a({inst[31:25], inst[14:12], inst[6:0]}), .b(17'h3b3), .eq(is_and));  // open: gt, lt
  Priority_Encoder #(.select(5)) priority_encoder_1 (
    .in0(is_add), .in1(is_mul), .in2(is_sub), .in3(is_sll), .in4(is_mulh), .in5(is_mulhu), .in6(is_slt),
    .in7(is_xor), .in8(is_srl), .in9(is_sra), .in10(is_or), .in11(is_and), .in12(is_lb), .in13(is_lh),
    .in14(is_lw), .in15(is_addi), .in16(is_slli), .in17(is_slti), .in18(is_xori), .in19(is_srli),
    .in20(is_srai), .in21(is_ori), .in22(is_andi), .in23(is_sb), .in24(is_sh), .in25(is_sw), .in26(is_beq),
    .in27(is_bne), .in28(is_blt), .in29(is_bge), .in30(is_bltu), .in31(is_bgeu),
    .out(priority_encoder_1_out), .gs(pri1_on));  // open: en_out, en_in
  Priority_Encoder priority_encoder_2 (
    .in1(is_auipc), .in2(is_lui), .in3(is_jal), .in4(is_jalr), .in5(is_csrw), .in6(is_csrwi),
    .out(priority_encoder_2_out));  // open: in0, in7, en_in, gs, en_out
  assign pri_out = {{1{1'b0}}, priority_encoder_1_out};  // Bit_Extender bit_extender_2
  assign bit_extender_3_out = {{3{1'b0}}, priority_encoder_2_out};  // Bit_Extender bit_extender_3
  BitSelector #(.width(3)) bitselector_1 (.in(inst[14:12]), .out(bitselector_1_out), .sel(2'b00));
  Adder #(.width(6)) adder_1 (.a(bit_extender_3_out), .b(6'b011111), .out(pri_out2));  // open: cin, cout
  BitSelector #(.width(7)) bitselector_2 (.in(opcode), .out(bitselector_2_out), .sel(3'b110));
  not not_1 (not_1_out, bitselector_3_out);
  BitSelector #(.width(7)) bitselector_3 (.in(opcode), .out(bitselector_3_out), .sel(3'b100));
  not not_2 (not_2_out, bitselector_4_out);
  BitSelector #(.width(3)) bitselector_4 (.in(inst[14:12]), .out(bitselector_4_out), .sel(2'b10));
  xor xor_1 (xor_1_out, bitselector_1_out, BrEq);
  and and_1 (and_1_out, bitselector_2_out, not_1_out);
  xor xor_2 (xor_2_out, BrLt, bitselector_1_out);
  and and_2 (and_2_out, not_2_out, xor_1_out);
  Multiplexer #(.enable("false"), .width(6)) multiplexer_1 (.in0(pri_out2), .in1(pri_out), .out(ROM_in), .sel(pri1_on));
  and and_3 (and_3_out, xor_2_out, bitselector_4_out);
  or or_1 (or_1_out, and_3_out, and_2_out);
  BitSelector #(.width(7)) bitselector_5 (.in(opcode), .out(bitselector_5_out), .sel(3'b010));
  or or_2 (or_2_out, or_1_out, bitselector_5_out);
  and and_4 (PCSel, and_1_out, or_2_out);

  // Other names for the same wires on the sheet: itype[9:0] = {inst[14:12], inst[6:0]};
  //   rtype[16:0] = {inst[31:25], inst[14:12], inst[6:0]}; func3[2:0] = inst[14:12]; func7[6:0] = inst[31:25]

  // Notes on the sheet:
  //   INPUTS to your circuit
  //   Connect ROM Input here ->
  //   itype shit is just func3+opcode
  //   rtype shit is funct7+func3+opcode
  //   contents of rom_1 (hex, n*v repeats v):
  //   8004 8104 8184 8024 8124 8164 8044 8084 80a4 81a4 80c4 80e4 9200 9200 9200 9204 9224 9244 9284 92a4
  //   93a4 92c4 92e4 3210 3210 3210 4*2600 2e00 2e00 d604 d3e4 c608 9208 8011 e213
  //   ROM FOR CONTROL LOGIC
  //   DON'T CHANGE THE LOCATIONS OF THE INPUTS AND OUTPUTS!
  //   OUTPUT from your circuit
  //   CLOSE
  //   WIRE
  //   TO
  //   USE
  //   ROM
  //   Reminder: Use combinational logic for PCSel
endmodule
