// Logisim project cpu.circ as structural Verilog: 1 circuit, main circuit cpu
module cpu (
  input  clk,
  input  [31:0] INSTRUCTION,
  input  [31:0] MEM_READ_DATA,
  output [31:0] MEM_WRITE_ADDRESS,
  output [31:0] PROGRAM_COUNTER,
  output [31:0] ra,
  output [31:0] sp,
  output [31:0] t0,
  output [31:0] t1,
  output [31:0] t2,
  output [31:0] s0,
  output [31:0] s1,
  output [31:0] a0,
  output [31:0] tohost,
  output [3:0] MEM_WRITE_ENABLE,
  output [31:0] MEM_WRITE_DATA
);

  wire ASel, BrEq, BrLt, BrUn, BSel, CSRSel, CSRWen, is_lb, is_lh, is_lw, is_sb, is_sh, is_sw, MemRW, PCSel,
       RegWEn;
  wire [1:0] bot2bits, load_sel, store_sel, WBSel;
  wire [2:0] ImmSel;
  wire [3:0] ALUSel, MEM_WRITE_SW, sb_out_mask, sh_out_mask;
  wire [7:0] sb00;
  wire [11:0] CSR_address;
  wire [15:0] sh00;
  wire [19:0] inst;
  wire [31:0] A, adder_1_out, adder_2_out, B, CSR_din, imm_out, lb00, lb01, lb10, lb11, lb_out, lh00, lh10,
       lh_out, mem_data_prc, multiplexer_1_out, multiplexer_3_out, multiplexer_9_out, multiplexer_10_out,
       PROGRAM_COUNTER_t, sb_out, sh_out, Write_Data;

  Adder #(.width(32)) adder_1 (.a(PROGRAM_COUNTER), .b(32'h4), .out(adder_1_out));  // open: cin, cout
  Register #(.width(32)) PC (.D(multiplexer_1_out), .clk(clk), .Q(PROGRAM_COUNTER));  // open: en, clr
  Multiplexer #(.enable("false"), .width(32)) multiplexer_1 (
    .in0(adder_1_out), .in1(MEM_WRITE_ADDRESS), .out(multiplexer_1_out), .sel(PCSel));
  Register #(.width(32)) register_1 (.D(PROGRAM_COUNTER), .en(1'b1), .clk(clk), .Q(PROGRAM_COUNTER_t));  // open: clr
  control_logic control_logic_1 (
    .CSRWen(CSRWen), .PCSel(PCSel), .RegWEn(RegWEn), .ImmSel(ImmSel), .BrUn(BrUn), .ASel(ASel), .BSel(BSel),
    .ALUSel(ALUSel), .MemRW(MemRW), .WBSel(WBSel), .CSRSel(CSRSel), .inst({CSR_address, inst}), .BrEq(BrEq),
    .BrLt(BrLt));
  Multiplexer #(.enable("false"), .select(2), .width(32)) multiplexer_2 (
    .in0(sb_out), .in1(sh_out), .in2(B), .out(MEM_WRITE_DATA), .sel(store_sel));  // open: in3
  Multiplexer #(.enable("false"), .width(32)) multiplexer_3 (
    .in0(INSTRUCTION), .in1(32'h13), .out(multiplexer_3_out), .sel(PCSel));
  imm_gen imm_gen_1 (.inst({CSR_address, inst}), .ImmSel(ImmSel), .imm(imm_out));
  Bit_Extender #(.in_width(32), .out_width(8)) bit_extender_1 (.in(B), .out(sb00));
  Bit_Extender #(.in_width(32)) bit_extender_2 (.in(B), .out(sh00));
  Multiplexer #(.enable("false"), .select(2), .width(32)) multiplexer_4 (
    .in0({{24{1'b0}}, sb00}), .in1({{16{1'b0}}, sb00, {8{1'b0}}}), .in2({{8{1'b0}}, sb00, {16{1'b0}}}),
    .in3({sb00, {24{1'b0}}}), .out(sb_out), .sel(bot2bits));
  Multiplexer #(.enable("false"), .select(2), .width(32)) multiplexer_5 (
    .in0({{16{1'b0}}, sh00}), .in2({sh00, {16{1'b0}}}), .out(sh_out), .sel(bot2bits));  // open: in1, in3
  Register #(.width(32)) register_2 (
    .D(multiplexer_3_out), .en(1'b1), .clk(clk), .Q({CSR_address, inst}));  // open: clr
  regfile regfile_1 (
    .rs1(inst[19:15]), .rs2(CSR_address[4:0]), .rd(inst[11:7]), .Write_Data(Write_Data), .RegWEn(RegWEn),
    .clk(clk), .ra(ra), .sp(sp), .t0(t0), .t1(t1), .t2(t2), .s0(s0), .s1(s1), .a0(a0), .Read_Data_1(A),
    .Read_Data_2(B));
  branch_comp branch_comp_1 (.rs1(A), .rs2(B), .BrUn(BrUn), .BrEq(BrEq), .BrLt(BrLt));
  Comparator #(.width(10)) comparator_1 (.a({inst[14:12], inst[6:0]}), .b(10'h23), .eq(is_sb));  // open: gt, lt
  Comparator #(.width(10)) comparator_2 (.a({inst[14:12], inst[6:0]}), .b(10'ha3), .eq(is_sh));  // open: gt, lt
  Comparator #(.width(10)) comparator_3 (.a({inst[14:12], inst[6:0]}), .b(10'h123), .eq(is_sw));  // open: gt, lt
  Priority_Encoder #(.select(2)) priority_encoder_1 (
    .in0(is_sb), .in1(is_sh), .in2(is_sw), .out(store_sel));  // open: in3, gs, en_out, en_in
  Multiplexer #(.enable("false"), .select(2), .width(4)) multiplexer_6 (
    .in0(4'b0001), .in1(4'b0010), .in2(4'b0100), .in3(4'b1000), .out(sb_out_mask), .sel(bot2bits));
  Multiplexer #(.enable("false"), .select(2), .width(4)) multiplexer_7 (
    .in0(4'b0011), .in1(4'b0000), .in2(4'b1100), .in3(4'b0000), .out(sh_out_mask), .sel(bot2bits));
  Multiplexer #(.enable("false"), .select(2), .width(4)) multiplexer_8 (
    .in0(sb_out_mask), .in1(sh_out_mask), .in2(4'b1111), .out(MEM_WRITE_SW), .sel(store_sel));  // open: in3
  Multiplexer #(.enable("false"), .width(32)) multiplexer_9 (
    .in0(A), .in1(PROGRAM_COUNTER_t), .out(multiplexer_9_out), .sel(ASel));
  Multiplexer #(.enable("false"), .width(32)) multiplexer_10 (
    .in0(B), .in1(imm_out), .out(multiplexer_10_out), .sel(BSel));
  alu alu_1 (.Result(MEM_WRITE_ADDRESS), .A(multiplexer_9_out), .B(multiplexer_10_out), .ALUSel(ALUSel));
  Multiplexer #(.enable("false"), .width(32)) multiplexer_11 (.in0(A), .in1(imm_out), .out(CSR_din), .sel(CSRSel));
  // csr csr_1: pin names not known; wires that end beside it: CSR_address, CSR_din, CSRWen, clk, tohost
  Multiplexer #(.enable("false"), .width(4)) multiplexer_12 (
    .in0(4'b0000), .in1(MEM_WRITE_SW), .out(MEM_WRITE_ENABLE), .sel(MemRW));
  Adder #(.width(32)) adder_2 (.a(PROGRAM_COUNTER_t), .b(32'h4), .out(adder_2_out));  // open: cin, cout
  Multiplexer #(.enable("false"), .select(2), .width(32)) multiplexer_13 (
    .in0(mem_data_prc), .in1(MEM_WRITE_ADDRESS), .in2(adder_2_out), .out(Write_Data), .sel(WBSel));  // open: in3
  Comparator #(.width(10)) comparator_4 (.a({inst[14:12], inst[6:0]}), .b(10'h3), .eq(is_lb));  // open: gt, lt
  Comparator #(.width(10)) comparator_5 (.a({inst[14:12], inst[6:0]}), .b(10'h83), .eq(is_lh));  // open: gt, lt
  Comparator #(.width(10)) comparator_6 (.a({inst[14:12], inst[6:0]}), .b(10'h103), .eq(is_lw));  // open: gt, lt
  Priority_Encoder #(.select(2)) priority_encoder_2 (
    .in0(is_lb), .in1(is_lh), .in2(is_lw), .out(load_sel));  // open: in3, gs, en_out, en_in
  Bit_Extender #(.in_width(32), .out_width(2), .\type ("zero")) bit_extender_3 (.in(MEM_WRITE_ADDRESS), .out(bot2bits));
  assign lb00 = {{24{MEM_READ_DATA[7]}}, MEM_READ_DATA[7:0]};  // Bit_Extender bit_extender_4
  assign lb01 = {{24{MEM_READ_DATA[15]}}, MEM_READ_DATA[15:8]};  // Bit_Extender bit_extender_5
  assign lb10 = {{24{MEM_READ_DATA[23]}}, MEM_READ_DATA[23:16]};  // Bit_Extender bit_extender_6
  assign lb11 = {{24{MEM_READ_DATA[31]}}, MEM_READ_DATA[31:24]};  // Bit_Extender bit_extender_7
  assign lh00 = {{16{MEM_READ_DATA[15]}}, MEM_READ_DATA[15:0]};  // Bit_Extender bit_extender_8
  assign lh10 = {{16{MEM_READ_DATA[31]}}, MEM_READ_DATA[31:16]};  // Bit_Extender bit_extender_9
  Multiplexer #(.enable("false"), .select(2), .width(32)) multiplexer_14 (
    .in0(lb00), .in1(lb01), .in2(lb10), .in3(lb11), .out(lb_out), .sel(bot2bits));
  Multiplexer #(.enable("false"), .select(2), .width(32)) multiplexer_15 (
    .in0(lh00), .in2(lh10), .out(lh_out), .sel(bot2bits));  // open: in1, in3
  Multiplexer #(.enable("false"), .select(2), .width(32)) multiplexer_16 (
    .in0(lb_out), .in1(lh_out), .in2(MEM_READ_DATA), .out(mem_data_prc), .sel(load_sel));  // open: in3

  // Other names for the same wires on the sheet: ALU_out[31:0] = MEM_WRITE_ADDRESS;
  //   INSTRUCTION_t[31:0] = {CSR_address, inst}; rd[4:0] = inst[11:7]; rs1[4:0] = inst[19:15];
  //   inst[31:20] = CSR_address; rs2[4:0] = CSR_address[4:0]; itype[9:0] = {inst[14:12], inst[6:0]};
  //   lw_out[31:0] = MEM_READ_DATA; sb01[15:8] = sb00; sb10[23:16] = sb00; sb11[31:24] = sb00; sh10[31:16] = sh00;
  //   sw_00[31:0] = B; sw_out[31:0] = B

  // Notes on the sheet:
  //   Output to IMEM
  //   IMEM (do **NOT** move this)
  //   Inputs from IMEM
  //   It is OK to move the PC, RegFile, ALU, MEM, Branch Comp, Imm Gen, and Control Logic to wherever is most convenient for you when constructing your CPU, and to delete this text
  //   Inputs/Outputs for testing. Do **NOT** move these.
  //   Outputs To DMEM
  //   DMEM (do **NOT** move this)
  //   Inputs From DMEM
endmodule
