// Logisim project imm-gen.circ as structural Verilog: 1 circuit, main circuit imm_gen
module imm_gen (
  input  [31:0] inst,
  input  [2:0] ImmSel,
  output [31:0] imm
);

  wire [31:0] btype, ctype, itype, jtype, stype;

  Multiplexer #(.enable("false"), .select(3), .width(32)) multiplexer_1 (
    .in1(itype), .in2(btype), .in3(stype), .in4(jtype), .in5({inst[31:12], {12{1'b0}}}), .in6(ctype),
    .out(imm), .sel(ImmSel));  // open: in0, in7
  assign itype = {{20{inst[31]}}, inst[31:20]};  // Bit_Extender bit_extender_1
  assign ctype = {{27{1'b0}}, inst[19:15]};  // Bit_Extender bit_extender_2
  assign stype = {{20{inst[31]}}, {inst[31:25], inst[11:7]}};  // Bit_Extender bit_extender_3
  assign btype = {{19{inst[31]}}, {inst[31], inst[7], inst[30:25], inst[11:8], 1'b0}};  // Bit_Extender bit_extender_4
  assign jtype = {{11{inst[31]}}, {inst[31], inst[19:12], inst[20], inst[30:21], 1'b0}};  // Bit_Extender bit_extender_5

  // Other names for the same wires on the sheet: utype[31:12] = inst[31:12]

  // Notes on the sheet:
  //   INPUTS to your circuit
  //   DON'T CHANGE THE LOCATIONS OF THE INPUTS AND OUTPUTS!
  //   OUTPUT from your circuit
endmodule
