// Logisim project regfile.circ as structural Verilog: 1 circuit, main circuit regfile
module regfile (
  input  [4:0] rs1,
  input  [4:0] rs2,
  input  [4:0] rd,
  input  [31:0] Write_Data,
  input  RegWEn,
  input  clk,
  output [31:0] ra,
  output [31:0] sp,
  output [31:0] t0,
  output [31:0] t1,
  output [31:0] t2,
  output [31:0] s0,
  output [31:0] s1,
  output [31:0] a0,
  output [31:0] Read_Data_1,
  output [31:0] Read_Data_2
);

  wire a0_in, a1_in, a2_in, a3_in, a4_in, a5_in, a6_in, a7_in, gp_in, ra_in, s0_in, s1_in, s2_in, s3_in,
       s4_in, s5_in, s6_in, s7_in, s8_in, s9_in, s10_in, s11_in, sp_in, t0_in, t1_in, t2_in, t3_in, t4_in,
       t5_in, t6_in, tp_in;
  wire [31:0] a1, a2, a3, a4, a5, a6, a7, gp, s2, s3, s4, s5, s6, s7, s8, s9, s10, s11, t3, t4, t5, t6, tp,
       x0;

  Demultiplexer #(.enable("false"), .select(5)) demultiplexer_1 (
    .out1(ra_in), .out2(sp_in), .out3(gp_in), .out4(tp_in), .out5(t0_in), .out6(t1_in), .out7(t2_in),
    .out8(s0_in), .out9(s1_in), .out10(a0_in), .out11(a1_in), .out12(a2_in), .out13(a3_in), .out14(a4_in),
    .out15(a5_in), .out16(a6_in), .out17(a7_in), .out18(s2_in), .out19(s3_in), .out20(s4_in), .out21(s5_in),
    .out22(s6_in), .out23(s7_in), .out24(s8_in), .out25(s9_in), .out26(s10_in), .out27(s11_in),
    .out28(t3_in), .out29(t4_in), .out30(t5_in), .out31(t6_in), .in(RegWEn), .sel(rd));  // open: out0
  Register #(.width(32)) register_1 (.D({32{1'b0}}), .clk(clk), .Q(x0));  // open: en, clr
  Register #(.width(32)) register_2 (.D(Write_Data), .en(ra_in), .clk(clk), .Q(ra));  // open: clr
  Register #(.width(32)) register_3 (.D(Write_Data), .en(sp_in), .clk(clk), .Q(sp));  // open: clr
  Register #(.width(32)) register_4 (.D(Write_Data), .en(gp_in), .clk(clk), .Q(gp));  // open: clr
  Register #(.width(32)) register_5 (.D(Write_Data), .en(tp_in), .clk(clk), .Q(tp));  // open: clr
  Register #(.width(32)) register_6 (.D(Write_Data), .en(t0_in), .clk(clk), .Q(t0));  // open: clr
  Register #(.width(32)) register_7 (.D(Write_Data), .en(t1_in), .clk(clk), .Q(t1));  // open: clr
  Register #(.width(32)) register_8 (.D(Write_Data), .en(t2_in), .clk(clk), .Q(t2));  // open: clr
  Register #(.width(32)) register_9 (.D(Write_Data), .en(a6_in), .clk(clk), .Q(a6));  // open: clr
  Register #(.width(32)) register_10 (.D(Write_Data), .en(a7_in), .clk(clk), .Q(a7));  // open: clr
  Register #(.width(32)) register_11 (.D(Write_Data), .en(s2_in), .clk(clk), .Q(s2));  // open: clr
  Register #(.width(32)) register_12 (.D(Write_Data), .en(s3_in), .clk(clk), .Q(s3));  // open: clr
  Register #(.width(32)) register_13 (.D(Write_Data), .en(s4_in), .clk(clk), .Q(s4));  // open: clr
  Register #(.width(32)) register_14 (.D(Write_Data), .en(s5_in), .clk(clk), .Q(s5));  // open: clr
  Register #(.width(32)) register_15 (.D(Write_Data), .en(s6_in), .clk(clk), .Q(s6));  // open: clr
  Register #(.width(32)) register_16 (.D(Write_Data), .en(s7_in), .clk(clk), .Q(s7));  // open: clr
  Register #(.width(32)) register_17 (.D(Write_Data), .en(s0_in), .clk(clk), .Q(s0));  // open: clr
  Register #(.width(32)) register_18 (.D(Write_Data), .en(s1_in), .clk(clk), .Q(s1));  // open: clr
  Register #(.width(32)) register_19 (.D(Write_Data), .en(a0_in), .clk(clk), .Q(a0));  // open: clr
  Register #(.width(32)) register_20 (.D(Write_Data), .en(a1_in), .clk(clk), .Q(a1));  // open: clr
  Register #(.width(32)) register_21 (.D(Write_Data), .en(a2_in), .clk(clk), .Q(a2));  // open: clr
  Register #(.width(32)) register_22 (.D(Write_Data), .en(a3_in), .clk(clk), .Q(a3));  // open: clr
  Register #(.width(32)) register_23 (.D(Write_Data), .en(a4_in), .clk(clk), .Q(a4));  // open: clr
  Register #(.width(32)) register_24 (.D(Write_Data), .en(a5_in), .clk(clk), .Q(a5));  // open: clr
  Register #(.width(32)) register_25 (.D(Write_Data), .en(s8_in), .clk(clk), .Q(s8));  // open: clr
  Register #(.width(32)) register_26 (.D(Write_Data), .en(s9_in), .clk(clk), .Q(s9));  // open: clr
  Register #(.width(32)) register_27 (.D(Write_Data), .en(s10_in), .clk(clk), .Q(s10));  // open: clr
  Register #(.width(32)) register_28 (.D(Write_Data), .en(s11_in), .clk(clk), .Q(s11));  // open: clr
  Register #(.width(32)) register_29 (.D(Write_Data), .en(t3_in), .clk(clk), .Q(t3));  // open: clr
  Register #(.width(32)) register_30 (.D(Write_Data), .en(t4_in), .clk(clk), .Q(t4));  // open: clr
  Register #(.width(32)) register_31 (.D(Write_Data), .en(t5_in), .clk(clk), .Q(t5));  // open: clr
  Register #(.width(32)) register_32 (.D(Write_Data), .en(t6_in), .clk(clk), .Q(t6));  // open: clr
  Multiplexer #(.enable("false"), .select(5), .width(32)) multiplexer_1 (
    .in0(x0), .in1(ra), .in2(sp), .in3(gp), .in4(tp), .in5(t0), .in6(t1), .in7(t2), .in8(s0), .in9(s1),
    .in10(a0), .in11(a1), .in12(a2), .in13(a3), .in14(a4), .in15(a5), .in16(a6), .in17(a7), .in18(s2),
    .in19(s3), .in20(s4), .in21(s5), .in22(s6), .in23(s7), .in24(s8), .in25(s9), .in26(s10), .in27(s11),
    .in28(t3), .in29(t4), .in30(t5), .in31(t6), .out(Read_Data_1), .sel(rs1));
  Multiplexer #(.enable("false"), .select(5), .width(32)) multiplexer_2 (
    .in0(x0), .in1(ra), .in2(sp), .in3(gp), .in4(tp), .in5(t0), .in6(t1), .in7(t2), .in8(s0), .in9(s1),
    .in10(a0), .in11(a1), .in12(a2), .in13(a3), .in14(a4), .in15(a5), .in16(a6), .in17(a7), .in18(s2),
    .in19(s3), .in20(s4), .in21(s5), .in22(s6), .in23(s7), .in24(s8), .in25(s9), .in26(s10), .in27(s11),
    .in28(t3), .in29(t4), .in30(t5), .in31(t6), .out(Read_Data_2), .sel(rs2));

  // Other names for the same wires on the sheet: read_data1[31:0] = Read_Data_1; read_data2[31:0] = Read_Data_2;
  //   read_reg1[4:0] = rs1; read_reg2[4:0] = rs2; write_en = RegWEn; write_reg[4:0] = rd

  // Notes on the sheet:
  //   INPUTS to your circuit
  //   DON'T CHANGE THE LOCATIONS OF THE INPUTS AND OUTPUTS!
  //   These are DEBUG/TEST outputs from your circuit.
  //   OUTPUTS from your circuit
endmodule
