// Logisim project cpu-store_load.circ as structural Verilog: 1 circuit, main circuit run_main
module run_main (
  output [31:0] ra,
  output [31:0] sp,
  output [31:0] t0,
  output [31:0] t1,
  output [31:0] t2,
  output [31:0] s0,
  output [31:0] s1,
  output [31:0] a0,
  output [31:0] Requested_Address,
  output [31:0] Requested_Instruction,
  output [15:0] Time_Step,
  output halt
);

  wire clk;

  Clock clock_1 (.out(clk));
  // Probe on Requested_Address
  // cpu_harness cpu_harness_1: pin names not known; wires that end beside it: Requested_Instruction, clk, Requested_Address, ra, sp, t0, t1, t2, s0, s1, a0
  ROM #(.addrWidth(14), .dataWidth(32)) rom_1 (.addr(Requested_Address[15:2]), .data(Requested_Instruction));
  // Probe on Requested_Instruction
  Counter #(.max('hffff), .width(16)) counter_1 (.clk(clk), .Q(Time_Step));  // open: clr, load, up, count, D, carry
  Comparator #(.width(16)) comparator_1 (.a(Time_Step), .b(16'hb5), .eq(halt));  // open: gt, lt

  // Other names for the same wires on the sheet: INSTRUCTION[31:0] = Requested_Instruction;
  //   PROGRAM_COUNTER[31:0] = Requested_Address

  // Notes on the sheet:
  //   contents of rom_1 (hex, n*v repeats v):
  //   F8010113 12023 112223 212423 312623 412823 512A23 612C23 712E23 2812023 2912223 2A12423 2B12623
  //   2C12823 2D12A23 2E12C23 2F12E23 5012023 5112223 5212423 5312623 5412823 5512A23 5612C23 5712E23
  //   7812023 7912223 7A12423 7B12623 7C12823 7D12A23 7E12C23 7F12E23 12003 412083 812103 C12183 1012203
  //   1412283 1812303 1C12383 2012403 2412483 2812503 2C12583 3012603 3412683 3812703 3C12783 4012803
  //   4412883 4812903 4C12983 5012A03 5412A83 5812B03 5C12B83 6012C03 6412C83 6812D03 6C12D83 7012E03
  //   7412E83 7812F03 7C12F83 8010113 FFC10113 110023 10083 410113 F8010113 11023 111223 211423 311623
  //   411823 511A23 611C23 711E23 2811023 2911223 2A11423 2B11623 2C11823 2D11A23 2E11C23 2F11E23 5011023
  //   5111223 5211423 5311623 5411823 5511A23 5611C23 5711E23 7811023 7911223 7A11423 7B11623 7C11823
  //   7D11A23 7E11C23 7F11E23 11003 411083 811103 C11183 1011203 1411283 1811303 1C11383 2011403 2411483
  //   2811503 2C11583 3011603 3411683 3811703 3C11783 4011803 4411883 4811903 4C11983 5011A03 5411A83
  //   5811B03 5C11B83 6011C03 6411C83 6811D03 6C11D83 7011E03 7411E83 7811F03 7C11F83 8010113 500513
  //   FFC10113 A12023 12503 410113 3E800513 44C00593 4B000613 100293 FE550E23 FE550EA3 FE550F23 FE550FA3
  //   550023 5500A3 550123 5501A3 550223 FE559E23 FE559F23 559023 559123 559223 FE562E23 562023 562223
  //   FFC50483 FFD50483 FFE50483 FFF50483 50483 150483 250483 350483 450483 FFC59483 FFE59483 59483 259483
  //   459483 FFC62483 62483 462483
  //   Instruction Memory
  //   Halts Execution After Constant # of Clock Cycles
  //   Constant
endmodule
